# Fritzing sketch Diagrama (saved by Fritzing 0.9.3b)
circuit board: 8.58772cm x 4.88148cm
breadboards: 2

parts:
  Componente1 = Logic Level Converter
  Componente2 = SparkFun ESP8266 Thing
  J1 = Piezo Speaker
  J2 = screw terminal, 3 pins
  J3 = screw terminal, 3 pins
  J4 = screw terminal, 3 pins
  Q1 = PNP-Transistor [package="TO92 [THT]"]
  J5 = Screw terminal - 2 pins [package=THT]
  J6 = Screw terminal - 2 pins [package=THT]
  J7 = Screw terminal - 2 pins [package=THT]
  NeoPixel = screw terminal, 3 pins [part_number=NeoPixel]
  LED2 = smd LED [color="Blue (470nm)" package="1206 [SMD]"]
  R3 = Resistor [tolerance=±5% resistance=330 package="1206 [SMD]"]
  LED3 = smd LED [color="Green (555nm)" package="1206 [SMD]"]
  R4 = Resistor [tolerance=±5% resistance=220 package="1206 [SMD]"]
  R1 = Resistor [tolerance=±5% resistance=330 package="1206 [SMD]"]
  LED1 = smd LED [color="Red (633nm)" package="1206 [SMD]"]
  R2 = Resistor [tolerance=±5% resistance=330 package="1206 [SMD]"]

nets:
  N1: Componente1.TX2_LV, Componente2.GPIO16
  N2: Componente1.RX2_LV, Componente2.GPIO12
  GND: Componente1.GND, Componente2.GND, J2.pin1, J4.pin1, Q1.E, NeoPixel.pin1, R3.Pin_1, R1.Pin_1, R2.Pin_1
  N3: Componente1.LV, Componente2.VCC, J1.pin2
  N4: Componente1.RX_LV, Componente2.GPIO13
  N5: Componente1.TX_HV, NeoPixel.pin2
  N6: Componente1.RX_HV, J2.pin3
  N7: Componente1.HV, Componente2.USBVCC, J3.pin2, NeoPixel.pin3
  N8: Componente1.RX2_HV, J2.pin2
  N9: Componente1.TX2_HV, J3.pin1
  N10: Componente2.GPIO14, R4.Pin_1
  N11: Componente2.VIN, J4.pin2
  N12: Componente2.GPIO0, J7.pin2, LED1.anode
  N13: Componente2.GPIO4, J6.pin2, LED2.anode
  N14: Componente2.GPIO15, J5.pin2, LED3.anode
  N15: J1.pin1, Q1.C
  N16: J3.pin3, J4.pin3
  N17: Q1.B, R4.Pin_0
  N18: J5.pin1, R3.Pin_0, LED3.cathode
  N19: J6.pin1, LED2.cathode, R2.Pin_0
  N20: J7.pin1, R1.Pin_0, LED1.cathode

notes:
  GND
  CLK
  SER
  5V
  12V
  LAT
  Poder
  Display
  Buzzer
  Led Indicador
  NEOPIXEL
  Data
