# Fritzing sketch DiagramaYoutube (saved by Fritzing 0.9.3b)
perfboards: 1

parts:
  Componente1 = SparkFun ESP8266 Thing  # not connected
  Componente2 = Logic Level Converter
  J1 = female pin header, 6 pins [form="♀ (female)"]
  J3 = female pin header, 10 pins [form="♀ (female)"]  # not connected
  J4 = female pin header, 10 pins [form="♀ (female)"]
  J2 = screw terminal, 3 pins

nets:
  N1: Componente2.GND, J1.pin6, J2.pin2
  N2: Componente2.HV, J1.pin2, J4.pin9, J2.pin3
  N3: Componente2.RX2_HV, J1.pin3
  N4: J1.pin1, J2.pin1

notes:
  12V
  5V
  SER
  CLK
  LAT
  GND
